# Fritzing sketch oleTSW_Controller-v0.1 (saved by Fritzing 1.0.4)
breadboards: 1

parts:
  MCU1 = Wemos Lolin32lite
  MCP23S17_01 = MCP23S17 I2C I/O Expander
  C05 = Ceramic Capacitor [capacitance=100nF voltage=35V package="100 mil [THT, multilayer]"]
  C07 = Ceramic Capacitor [capacitance=100nF voltage=35V package="100 mil [THT, multilayer]"]
  C08 = Ceramic Capacitor [capacitance=100nF voltage=35V package="100 mil [THT, multilayer]"]
  C06 = Ceramic Capacitor [capacitance=100nF voltage=35V package="100 mil [THT, multilayer]"]
  C03 = Ceramic Capacitor [capacitance=100nF voltage=35V package="100 mil [THT, multilayer]"]
  C04 = Ceramic Capacitor [capacitance=100nF voltage=35V package="100 mil [THT, multilayer]"]
  C02 = Ceramic Capacitor [capacitance=100nF voltage=35V package="100 mil [THT, multilayer]"]
  C01 = Ceramic Capacitor [capacitance=100nF voltage=35V package="100 mil [THT, multilayer]"]
  4609X-101_1 = IC, SIP package, 9 pins [chip_label=4609X-101]
  BTN_MCP_Reset = Pushbutton [package="[THT]"]
  R_MCP_Reset = Resistor [tolerance=±5% power=0.25W resistance=10k package=THT]
  btn01 = Camdenboss CTB0158-2 [part_number=CTB0158-2 package=THT]
  btn02 = Camdenboss CTB0158-2 [part_number=CTB0158-2 package=THT]
  btn03 = Camdenboss CTB0158-2 [part_number=CTB0158-2 package=THT]
  btn04 = Camdenboss CTB0158-2 [part_number=CTB0158-2 package=THT]
  btn05 = Camdenboss CTB0158-2 [part_number=CTB0158-2 package=THT]
  btn06 = Camdenboss CTB0158-2 [part_number=CTB0158-2 package=THT]
  btn07 = Camdenboss CTB0158-2 [part_number=CTB0158-2 package=THT]
  btn08 = Camdenboss CTB0158-2 [part_number=CTB0158-2 package=THT]
  C13 = Ceramic Capacitor [capacitance=100nF voltage=35V package="100 mil [THT, multilayer]"]
  C15 = Ceramic Capacitor [capacitance=100nF voltage=35V package="100 mil [THT, multilayer]"]
  C16 = Ceramic Capacitor [capacitance=100nF voltage=35V package="100 mil [THT, multilayer]"]
  C14 = Ceramic Capacitor [capacitance=100nF voltage=35V package="100 mil [THT, multilayer]"]
  C11 = Ceramic Capacitor [capacitance=100nF voltage=35V package="100 mil [THT, multilayer]"]
  C12 = Ceramic Capacitor [capacitance=100nF voltage=35V package="100 mil [THT, multilayer]"]
  C10 = Ceramic Capacitor [capacitance=100nF voltage=35V package="100 mil [THT, multilayer]"]
  C09 = Ceramic Capacitor [capacitance=100nF voltage=35V package="100 mil [THT, multilayer]"]
  4609X-101_2 = IC, SIP package, 9 pins [chip_label=4609X-101]
  btn09 = Camdenboss CTB0158-2 [part_number=CTB0158-2 package=THT]
  btn14 = Camdenboss CTB0158-2 [part_number=CTB0158-2 package=THT]
  btn16 = Camdenboss CTB0158-2 [part_number=CTB0158-2 package=THT]
  btn11 = Camdenboss CTB0158-2 [part_number=CTB0158-2 package=THT]
  btn15 = Camdenboss CTB0158-2 [part_number=CTB0158-2 package=THT]
  btn13 = Camdenboss CTB0158-2 [part_number=CTB0158-2 package=THT]
  btn12 = Camdenboss CTB0158-2 [part_number=CTB0158-2 package=THT]
  btn10 = Camdenboss CTB0158-2 [part_number=CTB0158-2 package=THT]
  C21 = Ceramic Capacitor [capacitance=100nF voltage=35V package="100 mil [THT, multilayer]"]
  C29 = Ceramic Capacitor [capacitance=100nF voltage=35V package="100 mil [THT, multilayer]"]
  C23 = Ceramic Capacitor [capacitance=100nF voltage=35V package="100 mil [THT, multilayer]"]
  C31 = Ceramic Capacitor [capacitance=100nF voltage=35V package="100 mil [THT, multilayer]"]
  C32 = Ceramic Capacitor [capacitance=100nF voltage=35V package="100 mil [THT, multilayer]"]
  C24 = Ceramic Capacitor [capacitance=100nF voltage=35V package="100 mil [THT, multilayer]"]
  C22 = Ceramic Capacitor [capacitance=100nF voltage=35V package="100 mil [THT, multilayer]"]
  C30 = Ceramic Capacitor [capacitance=100nF voltage=35V package="100 mil [THT, multilayer]"]
  C19 = Ceramic Capacitor [capacitance=100nF voltage=35V package="100 mil [THT, multilayer]"]
  C27 = Ceramic Capacitor [capacitance=100nF voltage=35V package="100 mil [THT, multilayer]"]
  C28 = Ceramic Capacitor [capacitance=100nF voltage=35V package="100 mil [THT, multilayer]"]
  C20 = Ceramic Capacitor [capacitance=100nF voltage=35V package="100 mil [THT, multilayer]"]
  C26 = Ceramic Capacitor [capacitance=100nF voltage=35V package="100 mil [THT, multilayer]"]
  C18 = Ceramic Capacitor [capacitance=100nF voltage=35V package="100 mil [THT, multilayer]"]
  C17 = Ceramic Capacitor [capacitance=100nF voltage=35V package="100 mil [THT, multilayer]"]
  C25 = Ceramic Capacitor [capacitance=100nF voltage=35V package="100 mil [THT, multilayer]"]
  4609X-101_4 = IC, SIP package, 9 pins [chip_label=4609X-101]
  4609X-101_3 = IC, SIP package, 9 pins [chip_label=4609X-101]
  btn17 = Camdenboss CTB0158-2 [part_number=CTB0158-2 package=THT]
  btn22 = Camdenboss CTB0158-2 [part_number=CTB0158-2 package=THT]
  btn25 = Camdenboss CTB0158-2 [part_number=CTB0158-2 package=THT]
  btn19 = Camdenboss CTB0158-2 [part_number=CTB0158-2 package=THT]
  btn29 = Camdenboss CTB0158-2 [part_number=CTB0158-2 package=THT]
  btn24 = Camdenboss CTB0158-2 [part_number=CTB0158-2 package=THT]
  btn32 = Camdenboss CTB0158-2 [part_number=CTB0158-2 package=THT]
  btn27 = Camdenboss CTB0158-2 [part_number=CTB0158-2 package=THT]
  btn30 = Camdenboss CTB0158-2 [part_number=CTB0158-2 package=THT]
  btn20 = Camdenboss CTB0158-2 [part_number=CTB0158-2 package=THT]
  btn21 = Camdenboss CTB0158-2 [part_number=CTB0158-2 package=THT]
  btn26 = Camdenboss CTB0158-2 [part_number=CTB0158-2 package=THT]
  btn28 = Camdenboss CTB0158-2 [part_number=CTB0158-2 package=THT]
  btn23 = Camdenboss CTB0158-2 [part_number=CTB0158-2 package=THT]
  btn31 = Camdenboss CTB0158-2 [part_number=CTB0158-2 package=THT]
  btn18 = Camdenboss CTB0158-2 [part_number=CTB0158-2 package=THT]
  MCP23S17_02 = MCP23S17 I2C I/O Expander
  C_MCP02 = Ceramic Capacitor [capacitance=100nF voltage=35V package="100 mil [THT, multilayer]"]
  C_MCP01 = Ceramic Capacitor [capacitance=100nF voltage=35V package="100 mil [THT, multilayer]"]

nets:
  GND: MCU1.pin_13, MCP23S17_01.VSS, MCP23S17_01.A0, MCP23S17_01.A1, MCP23S17_01.A2, C05.0, C07.0, C08.0, C06.0, C03.0, C04.0, C02.0, C01.0, BTN_MCP_Reset.Pin_1, BTN_MCP_Reset.Pin_2, btn01.pin1, btn02.pin1, btn03.pin1, btn04.pin1, btn05.pin1, btn06.pin1, btn07.pin1, btn08.pin1, C13.0, C15.0, C16.0, C14.0, C11.0, C12.0, C10.0, C09.0, btn09.pin1, btn14.pin1, btn16.pin1, btn11.pin1, btn15.pin1, btn13.pin1, btn12.pin1, btn10.pin1, C21.0, C29.0, C23.0, C31.0, C32.0, C24.0, C22.0, C30.0, C19.0, C27.0, C28.0, C20.0, C26.0, C18.0, C17.0, C25.0, btn17.pin1, btn22.pin1, btn25.pin1, btn19.pin1, btn29.pin1, btn24.pin1, btn32.pin1, btn27.pin1, btn30.pin1, btn20.pin1, btn21.pin1, btn26.pin1, btn28.pin1, btn23.pin1, btn31.pin1, btn18.pin1, MCP23S17_02.VSS, MCP23S17_02.A1, MCP23S17_02.A2, C_MCP02.0, C_MCP01.0
  CS: MCU1.pin_23, MCP23S17_01.CS, MCP23S17_02.CS
  CLK: MCU1.pin_24, MCP23S17_01.SCK, MCP23S17_02.SCK
  MOSI: MCU1.pin_25, MCP23S17_01.SI, MCP23S17_02.SI
  MISO: MCU1.pin_26, MCP23S17_01.SO, MCP23S17_02.SO
  VDD 3.3v: MCU1.pin_28, MCP23S17_01.VDD, 4609X-101_1.pin1, R_MCP_Reset.Pin_1, 4609X-101_2.pin1, 4609X-101_4.pin1, 4609X-101_3.pin1, MCP23S17_02.VDD, MCP23S17_02.A0, C_MCP02.1, C_MCP01.1
  N1: MCP23S17_01.GPB0, C09.1, 4609X-101_2.pin9, btn09.pin2
  N2: MCP23S17_01.GPB1, C10.1, 4609X-101_2.pin8, btn10.pin2
  N3: MCP23S17_01.GPB2, C11.1, 4609X-101_2.pin7, btn11.pin2
  N4: MCP23S17_01.GPB3, C12.1, 4609X-101_2.pin6, btn12.pin2
  N5: MCP23S17_01.GPB4, C13.1, 4609X-101_2.pin5, btn13.pin2
  N6: MCP23S17_01.GPB5, C14.1, 4609X-101_2.pin4, btn14.pin2
  N7: MCP23S17_01.GPB6, C15.1, 4609X-101_2.pin3, btn15.pin2
  N8: MCP23S17_01.GPB7, C16.1, 4609X-101_2.pin2, btn16.pin2
  MCP23S17_RESET: MCP23S17_01.RESET, BTN_MCP_Reset.Pin_4, R_MCP_Reset.Pin_0, MCP23S17_02.RESET
  N9: MCP23S17_01.GPA0, C01.1, 4609X-101_1.pin9, btn01.pin2
  N10: MCP23S17_01.GPA1, C02.1, 4609X-101_1.pin8, btn02.pin2
  N11: MCP23S17_01.GPA2, C03.1, 4609X-101_1.pin7, btn03.pin2
  N12: MCP23S17_01.GPA3, C04.1, 4609X-101_1.pin6, btn04.pin2
  N13: MCP23S17_01.GPA4, C05.1, 4609X-101_1.pin5, btn05.pin2
  N14: MCP23S17_01.GPA5, C06.1, 4609X-101_1.pin4, btn06.pin2
  N15: MCP23S17_01.GPA6, C07.1, 4609X-101_1.pin3, btn07.pin2
  N16: MCP23S17_01.GPA7, C08.1, 4609X-101_1.pin2, btn08.pin2
  N17: C21.1, 4609X-101_3.pin5, btn21.pin2, MCP23S17_02.GPA4
  N18: C29.1, 4609X-101_4.pin5, btn29.pin2, MCP23S17_02.GPB4
  N19: C23.1, 4609X-101_3.pin3, btn23.pin2, MCP23S17_02.GPA6
  N20: C31.1, 4609X-101_4.pin3, btn31.pin2, MCP23S17_02.GPB6
  N21: C32.1, 4609X-101_4.pin2, btn32.pin2, MCP23S17_02.GPB7
  N22: C24.1, 4609X-101_3.pin2, btn24.pin2, MCP23S17_02.GPA7
  N23: C22.1, 4609X-101_3.pin4, btn22.pin2, MCP23S17_02.GPA5
  N24: C30.1, 4609X-101_4.pin4, btn30.pin2, MCP23S17_02.GPB5
  N25: C19.1, 4609X-101_3.pin7, btn19.pin2, MCP23S17_02.GPA2
  N26: C27.1, 4609X-101_4.pin7, btn27.pin2, MCP23S17_02.GPB2
  N27: C28.1, 4609X-101_4.pin6, btn28.pin2, MCP23S17_02.GPB3
  N28: C20.1, 4609X-101_3.pin6, btn20.pin2, MCP23S17_02.GPA3
  N29: C26.1, 4609X-101_4.pin8, btn26.pin2, MCP23S17_02.GPB1
  N30: C18.1, 4609X-101_3.pin8, btn18.pin2, MCP23S17_02.GPA1
  N31: C17.1, 4609X-101_3.pin9, btn17.pin2, MCP23S17_02.GPA0
  N32: C25.1, 4609X-101_4.pin9, btn25.pin2, MCP23S17_02.GPB0

custom parts:
  Wemos Lolin32lite: Wemos Lolinlite32 wifi and blue tooth board based on the ESP-32 cpu, digital I/Os 19, analog inputs 6, clock 240mhz, Flash 4Mbytes, lipo battery charger (500ma connection broken out on breadboard but not pcb), usb.
  MCP23S17 I2C I/O Expander: The MCP23S17 uses fourspi pins , and in exchange gives you 16 general purpose pins. You can set each of 16 pins to be input, output, input with a pullup or open drain. There's even the ability to get an interrupt via an external pin when any of the inputs change so you don't have to keep polling the chip.
